# Fritzing sketch Sketch (saved by Fritzing 0.9.3b)
breadboards: 1

parts:
  PC817 = TLP621 [package=THT]
  R1 = Resistor [tolerance=±5% resistance=1k package=THT]
  R2 = Resistor [tolerance=±5% resistance=10k package=THT]
  Composant1 = Arduino Uno (Rev3)
  Power_plug1 = Power plug
  D1 = Rectifier Diode [part_number=1N4001 package="300 mil [THT]"]
  R4 = Resistor [tolerance=±5% resistance=4.7k package=THT]
  100mF = Tantalum Capacitor [capacitance=1mF voltage=25V package="100 mil [THT, tantalum]"]

nets (from the breadboard view):
  N1: PC817.Pin_1, R4.Pin_1
  N2: PC817.Pin_2, Power_plug1.GND
  N3: PC817.Pin_4, R2.Pin_0, Composant1.D13/SCK
  N4: PC817.Pin_3, Composant1.GND
  N5: R1.Pin_0, Power_plug1.VCC
  N6: R1.Pin_1, D1.anode
  N7: R2.Pin_1, Composant1.5V
  N8: D1.cathode, 100mF.-

notes:
  passage du 12vac à 5vcc
