# Fritzing sketch schema (saved by Fritzing 0.9.2b)
breadboards: 1

parts:
  R1 = Resistor [tolerance=±5% resistance=220 package=THT]
  R2 = Resistor [tolerance=±5% resistance=220 package=THT]
  R3 = Resistor [tolerance=±5% resistance=220 package=THT]
  R4 = Resistor [tolerance=±5% resistance=220 package=THT]
  S1 = Pushbutton [package="[THT]"]
  S2 = Pushbutton [package="[THT]"]
  S3 = Pushbutton [package="[THT]"]
  S4 = Pushbutton [package="[THT]"]
  R5 = Resistor [tolerance=±5% resistance=220 package=THT]
  R6 = Resistor [tolerance=±5% resistance=220 package=THT]
  Composant1 = Arduino Uno (Rev3)
  LED1 = LED - 5mm [color="Red (633nm)" package="5 mm [THT]"]
  LED2 = LED - 5mm [color="Red (633nm)" package="5 mm [THT]"]
  LED3 = LED - 5mm [color="Red (633nm)" package="5 mm [THT]"]
  LED4 = LED - 5mm [color="Red (633nm)" package="5 mm [THT]"]
  R8 = Resistor [tolerance=±5% resistance=220 package=THT]
  R9 = Resistor [tolerance=±5% resistance=220 package=THT]
  R10 = Resistor [tolerance=±5% resistance=220 package=THT]
  R11 = Resistor [tolerance=±5% resistance=220 package=THT]
  MIC1 = Microphone

nets:
  N1: R1.Pin_0, Composant1.5V
  N2: R1.Pin_1, R2.Pin_0, S1.Pin_3, S1.Pin_4
  N3: R2.Pin_1, R3.Pin_0, S2.Pin_3, S2.Pin_4
  N4: R3.Pin_1, R4.Pin_0, S3.Pin_3, S3.Pin_4
  N5: R4.Pin_1, S4.Pin_3, S4.Pin_4, R5.Pin_0
  N6: S1.Pin_1, S1.Pin_2, S2.Pin_1, S2.Pin_2, S3.Pin_1, S3.Pin_2, S4.Pin_1, S4.Pin_2, R6.Pin_0
  N7: R5.Pin_1, R6.Pin_1, Composant1.A1
  N8: Composant1.D8, MIC1.pin2
  N9: Composant1.D2, LED4.anode
  N10: Composant1.D3_PWM, LED3.anode
  N11: Composant1.D4, LED2.anode
  N12: Composant1.D5_PWM, LED1.anode
  N13: Composant1.GND, R8.Pin_1, R9.Pin_1, R10.Pin_1, R11.Pin_1, MIC1.pin1
  N14: LED1.cathode, R10.Pin_0
  N15: LED2.cathode, R9.Pin_0
  N16: LED3.cathode, R8.Pin_0
  N17: LED4.cathode, R11.Pin_0
